# Fritzing sketch Wire Diagram_updated (saved by Fritzing 0.9.3b)

parts:
  Part1 = Motor Driver 1A Dual TB6612FNG
  BAT1 = BC9VPC [package=bc9vpc]
  Nano = Arduino Nano (Rev3.0) (ICSP)
  S1 = Pololu QTR-8 Reflectabce Sensor array [package=THT]
  U1 = Mini-360 DC-DC Buck converter [package=THT]
  M2 = DC Motor
  M3 = DC Motor

nets:
  GND: Part1.GND, Nano.GND, S1.pin1, S1.pin15, U1.OUT-
  N1: Part1.B01, M2.pin_2
  N2: Part1.B02, M2.pin_1
  N3: Part1.A02, M3.pin_1
  N4: Part1.A01, M3.pin_2
  VCC: Part1.VCC, Nano.5V, S1.pin14, S1.pin22
  N5: Part1.VM, U1.OUT+
  N6: Part1.PWMA, Nano.D3
  N7: Part1.AIN2, Nano.D4
  N8: Part1.AIN1, Nano.D5
  N9: Part1.STBY, Nano.D6
  N10: Part1.BIN1, Nano.D7
  N11: Part1.BIN2, Nano.D8
  N12: Part1.PWMB, Nano.D9
  N13: BAT1.V+, U1.IN+
  N14: BAT1.V-, U1.IN-
  N15: Nano.D2, S1.pin13
  N16: Nano.A7, S1.pin5
  N17: Nano.A6, S1.pin6
  N18: Nano.A5, S1.pin7
  N19: Nano.A4, S1.pin8
  N20: Nano.A3, S1.pin9
  N21: Nano.A2, S1.pin10
  N22: Nano.A1, S1.pin11
  N23: Nano.A0, S1.pin12

custom parts:
  Mini-360 DC-DC Buck converter: Mini-360 DC-DC Buck converter. Tiny buck step down voltage converter, input voltage 4.75 to 23V output 1 to 17V adjustable. Available from ebay and the like.
